# Fritzing sketch morrigan_breadboard_full_sketch (saved by Fritzing 0.9.5d)
breadboards: 1

parts:
  Bauteil1 = ADS1115
  DS1 = DS18B20 1-Wire Temperature Sensor [part_number=DS18B20]
  Raspberry_Pi_1 = Raspberry Pi 3 [part_number=RPI-3-V1.2]
  S1 = PH meter [package=THT]
  S2 = PH meter [package=THT]
  S3 = PH meter [package=THT]
  S4 = PH meter [package=THT]

nets:
  VDD: Bauteil1.VDD, DS1.VDD, Raspberry_Pi_1.3v3, Raspberry_Pi_1.3V3, S1.pin2, S2.pin2, S3.pin2, S4.pin2
  GND: Bauteil1.GND, DS1.GND, Raspberry_Pi_1.GND, S1.pin3, S2.pin3, S3.pin3, S4.pin3
  N1: Bauteil1.SCL, Raspberry_Pi_1.GPIO3
  N2: Bauteil1.SDA, Raspberry_Pi_1.GPIO2
  N3: Bauteil1.A0, S2.pin1
  N4: Bauteil1.A1, S1.pin1
  N5: Bauteil1.A2, S3.pin1
  N6: Bauteil1.A3, S4.pin1
  N7: DS1.DQ, Raspberry_Pi_1.GPIO4

custom parts:
  ADS1115: ADC ADS1115
