# Fritzing sketch morrigan_pcb_full_sketch (saved by Fritzing 0.9.5d)

parts:
  JP1 = Header 4 [package=jst-4-pth]
  JP2 = Header 5x2 [package=2x5-raf]
  Raspberry_Pi_1 = Raspberry Pi 3 [part_number=RPI-3-V1.2]
  JP3 = Header 4 [package=jst-4-pth]
  JP4 = Header 4 [package=jst-4-pth]
  JP5 = Header 4 [package=jst-4-pth]
  DS1 = DS18B20 1-Wire Temperature Sensor [part_number=DS18B20]
  S1 = PH meter [package=THT]
  S2 = PH meter [package=THT]
  S3 = PH meter [package=THT]
  S4 = PH meter [package=THT]

nets:
  3V3: JP1.1, JP2.1, Raspberry_Pi_1.3v3, Raspberry_Pi_1.3V3, JP3.1, JP4.1, JP5.1, DS1.VDD, S1.pin2, S2.pin2, S3.pin2, S4.pin2
  GND: JP1.2, JP2.3, Raspberry_Pi_1.GND, JP3.2, JP4.2, JP5.2, DS1.GND, S1.pin3, S2.pin3, S3.pin3, S4.pin3
  N1: JP1.4, JP2.10, S1.pin1
  N2: JP2.4, JP5.4, S4.pin1
  N3: JP2.5, Raspberry_Pi_1.GPIO3
  N4: JP2.6, JP4.4, S3.pin1
  N5: JP2.7, Raspberry_Pi_1.GPIO2
  N6: JP2.8, JP3.4, S2.pin1
  N7: Raspberry_Pi_1.GPIO4, DS1.DQ
